// Logisim project compteur_bcd_4_bit.circ as structural Verilog: 1 circuit, main circuit main
module main (
  input  [3:0] D,
  input  load,
  input  inc,
  input  clk,
  input  rst
);

  wire and_1_out, comparator_1_eq, or_1_out;
  wire [3:0] adder_1_out, multiplexer_1_out, multiplexer_2_out, register_1_q;

  Adder #(.width(4)) adder_1 (.a(register_1_q), .b(4'b0001), .out(adder_1_out));  // open: cin, cout
  Multiplexer #(.width(4), .enable("false")) multiplexer_1 (
    .in0(adder_1_out), .in1(D), .out(multiplexer_1_out), .sel(load));
  and and_1 (and_1_out, comparator_1_eq, inc);
  Multiplexer #(.width(4), .enable("false")) multiplexer_2 (
    .in0(multiplexer_1_out), .in1(4'b0000), .out(multiplexer_2_out), .sel(and_1_out));
  or or_1 (or_1_out, load, inc);
  Register #(.width(4)) register_1 (.D(multiplexer_2_out), .en(or_1_out), .clk(clk), .Q(register_1_q), .clr(rst));
  Comparator #(.width(4)) comparator_1 (.a(register_1_q), .b(4'b1001), .eq(comparator_1_eq));  // open: gt, lt
  // Probe on comparator_1_eq
endmodule
