// Logisim project compteur_bcd_8bit_modp.circ as structural Verilog: 1 circuit, main circuit main
module main (
  input  clk,
  input  rst,
  input  [7:0] P,
  input  inc
);

  wire and_1_out, comparator_1_eq;
  wire [7:0] adder_1_out, multiplexer_1_out, register_1_q, subtractor_1_out;

  Adder adder_1 (.a(register_1_q), .b(8'h1), .out(adder_1_out));  // open: cin, cout
  Multiplexer #(.width(8), .enable("false")) multiplexer_1 (
    .in0(adder_1_out), .in1({8{1'b0}}), .out(multiplexer_1_out), .sel(and_1_out));
  and and_1 (and_1_out, inc, comparator_1_eq);
  Register register_1 (.D(multiplexer_1_out), .en(inc), .clk(clk), .Q(register_1_q), .clr(rst));
  Subtractor subtractor_1 (.a(P), .b(8'h1), .out(subtractor_1_out));  // open: bin, bout
  Comparator comparator_1 (.a(register_1_q), .b(subtractor_1_out), .eq(comparator_1_eq));  // open: gt, lt
  // Probe on register_1_q
  // Probe on comparator_1_eq
endmodule
