// Logisim project Multiplieur8x8_backup.circ as structural Verilog: 1 circuit, main circuit Multiplieur8x8
module Multiplieur8x8 (
  input  clk,
  input  rst,
  input  [7:0] A,
  input  [7:0] B,
  input  REQ,
  output ACK,
  output [15:0] RES
);

  wire bitselector_1_out, comparator_1_eq, undriven_4, undriven_6;
  wire [3:0] i_q, uc_mul_1_p8, undriven;
  wire [7:0] mB_q, shifter_1_out, undriven_2;
  wire [15:0] bit_extender_1_out, bit_extender_2_out, bit_extender_3_out, mA_q, multiplexer_1_out,
       shifter_2_out, uc_mul_1_p3, undriven_3, undriven_5;

  // FSM_Entity #(.content("state_machine UC_MUL @[88,45,800,500]{\n	in REQ[1]   @[88,161,32,15];\n	out ACK[1]   @[858,143,30,15];Memory[1]   @[839,336,49,15];sel_reg_write[1]   @[807,381,81,15];OP[4]   @[842,421,46,15];\n	codeWidth = 4;\n	reset = IDLE;\n	\n	state IDLE[\"0000\"]:\n	 	@[280,153,30,30]\n}")) uc_mul_1: pin names not known; wires that end beside it: A, B, uc_mul_1_p3, clk, rst, 1'b1, REQ, uc_mul_1_p8
  Register mB (.D(undriven_2), .clk(clk), .Q(mB_q), .clr(rst));  // open: en
  Register #(.width(16)) mA (.D(undriven_3), .clk(clk), .Q(mA_q), .clr(rst));  // open: en
  Register #(.width(4)) i (.D(undriven), .clk(clk), .Q(i_q), .clr(rst));  // open: en
  BitSelector bitselector_1 (.in(mB_q), .out(bitselector_1_out), .sel(3'b000));
  Shifter #(.shift("lr")) shifter_1 (.in(mB_q), .\dist (3'b001), .out(shifter_1_out));
  assign bit_extender_1_out = {{8{1'b0}}, mB_q};  // Bit_Extender bit_extender_1
  Shifter #(.width(16)) shifter_2 (.in(mA_q), .\dist (4'b0001), .out(shifter_2_out));
  Comparator #(.width(1)) comparator_1 (.a(bitselector_1_out), .b(undriven_4), .eq(comparator_1_eq));  // open: gt, lt
  assign bit_extender_2_out = {{8{1'b0}}, shifter_1_out};  // Bit_Extender bit_extender_2
  Multiplexer #(.width(16), .enable("false")) multiplexer_1 (
    .in0(bit_extender_1_out), .in1(mA_q), .out(multiplexer_1_out));  // open: sel
  assign bit_extender_3_out = {{15{1'b0}}, comparator_1_eq};  // Bit_Extender bit_extender_3
  Register #(.width(16)) ACC (.D(undriven_5), .en(undriven_6), .clk(clk), .Q(RES), .clr(rst));
  Multiplexer #(.select(4), .width(16), .enable("false")) multiplexer_2 (
    .in0(bit_extender_3_out), .in1(RES), .in2(multiplexer_1_out), .in3(shifter_2_out),
    .in4(bit_extender_2_out), .in5(bit_extender_2_out), .out(uc_mul_1_p3), .sel(uc_mul_1_p8));  // open: in6, in7, in8, in9, in10, in11, in12, in13, in14, in15
endmodule
