// Logisim project TestMultiplieur8x8.circ as structural Verilog: 1 circuit, main circuit TestMultiplieur8x8
module TestMultiplieur8x8 (
  input  rst,
  input  REQ,
  output ACK
);

  wire bin_to_7_segment_decoder_1_p7, clk_out;
  wire [7:0] SW_sw8;
  wire [15:0] bin_to_7_segment_decoder_1_p6;

  DipSwitch SW (
    .sw1(SW_sw8[7]), .sw2(SW_sw8[6]), .sw3(SW_sw8[5]), .sw4(SW_sw8[4]), .sw5(SW_sw8[3]), .sw6(SW_sw8[2]),
    .sw7(SW_sw8[1]), .sw8(SW_sw8[0]));
  // Probe on SW_sw8
  Clock clk (.out(clk_out));
  // Bin_to_7_Segment_decoder bin_to_7_segment_decoder_1: pin names not known; wires that end beside it: clk_out, rst, SW_sw8, REQ, ACK, bin_to_7_segment_decoder_1_p6, bin_to_7_segment_decoder_1_p7, bin_to_7_segment_decoder_1_p6[15:12]
  _7_Segment_Display Hex5 ();  // open: g, f, a, b, e, d, c, dp
  // Bin_to_7_Segment_decoder bin_to_7_segment_decoder_2: pin names not known; wires that end beside it: bin_to_7_segment_decoder_1_p6[11:8]
  _7_Segment_Display Hex4 ();  // open: g, f, a, b, e, d, c, dp
  // Probe on bin_to_7_segment_decoder_1_p7
  _7_Segment_Display Hex3 ();  // open: g, f, a, b, e, d, c, dp
  // Bin_to_7_Segment_decoder bin_to_7_segment_decoder_3: pin names not known; wires that end beside it: bin_to_7_segment_decoder_1_p6[7:4]
  // Probe on bin_to_7_segment_decoder_1_p6[7:4]
  _7_Segment_Display Hex2 ();  // open: g, f, a, b, e, d, c, dp
  // Bin_to_7_Segment_decoder bin_to_7_segment_decoder_4: pin names not known; wires that end beside it: bin_to_7_segment_decoder_1_p6[3:0]
endmodule
