// Logisim project chrono_debut.circ as structural Verilog: 1 circuit, main circuit main
module main (
  input  C,
  input  RST
);

  wire clk_out, d_ff_1_q, d_ff_2_q, d_ff_2_qn, or_1_out, xor_1_out;

  Clock clk (.out(clk_out));
  D_Flip_Flop d_ff_1 (.D(d_ff_2_qn), .clk(clk_out), .Q(d_ff_1_q), .reset(RST));  // open: Qn, preset
  // Probe on d_ff_1_q
  xor xor_1 (xor_1_out, d_ff_2_q, d_ff_1_q);
  D_Flip_Flop d_ff_2 (.D(or_1_out), .clk(clk_out), .Q(d_ff_2_q), .Qn(d_ff_2_qn), .reset(RST));  // open: preset
  or or_1 (or_1_out, xor_1_out, C);
  // Probe on d_ff_2_q
endmodule
