// Logisim project compteur_bcd.circ as structural Verilog: 1 circuit, main circuit main
module main (
  input  [3:0] D,
  input  load,
  input  inc,
  input  clk,
  input  rst
);

  wire or_1_out;
  wire [3:0] adder_1_out, multiplexer_1_out, register_1_q;

  Adder #(.width(4)) adder_1 (.a(register_1_q), .b(4'b0001), .out(adder_1_out));  // open: cin, cout
  Multiplexer #(.width(4), .enable("false")) multiplexer_1 (
    .in0(adder_1_out), .in1(D), .out(multiplexer_1_out), .sel(load));
  or or_1 (or_1_out, load, inc);
  Register #(.width(4)) register_1 (.D(multiplexer_1_out), .en(or_1_out), .clk(clk), .Q(register_1_q), .clr(rst));
endmodule
