// Logisim project Multiplieur8x8.circ as structural Verilog: 1 circuit, main circuit Multiplieur8x8
module Multiplieur8x8 (
  input  clk,
  input  rst,
  input  [7:0] A,
  input  [7:0] B,
  input  REQ,
  output ACK,
  output [15:0] RES
);

  wire bitselector_1_out, comparator_1_eq, uc_mul_1_p7, uc_mul_1_p8, undriven_2, undriven_3, undriven_5,
       undriven_6, undriven_7;
  wire [3:0] i_q, undriven_4;
  wire [7:0] mB_q, multiplexer_2_out, shifter_1_out, undriven;
  wire [15:0] adder_2_out, mA_q, multiplexer_1_out, multiplexer_3_out, shifter_2_out, uc_mul_1_p9;

  // FSM_Entity #(.content("state_machine UC_MUL @[88,45,800,500]{\n	in REQ[1]   @[88,161,32,15];\n	out ACK[1]   @[858,143,30,15];Memory[1]   @[839,336,49,15];sel_reg_write[1]   @[807,381,81,15];OP[4]   @[842,421,46,15];\n	codeWidth = 4;\n	reset = IDLE;\n	\n	state IDLE[\"0000\"]:\n	 	@[280,153,30,30]\n}")) uc_mul_1: pin names not known; wires that end beside it: A, B, clk, rst, 1'b1, REQ, uc_mul_1_p7, uc_mul_1_p8, uc_mul_1_p9
  Multiplexer #(.width(16), .enable("false")) multiplexer_1 (
    .in0(uc_mul_1_p9), .in1(shifter_2_out), .out(multiplexer_1_out), .sel(uc_mul_1_p8));
  Multiplexer #(.width(8), .enable("false")) multiplexer_2 (
    .in0(undriven), .in1(shifter_1_out), .out(multiplexer_2_out), .sel(undriven_3));
  Register mB (.D(multiplexer_2_out), .en(undriven_2), .clk(clk), .Q(mB_q), .clr(rst));
  Register #(.width(16)) mA (.D(multiplexer_1_out), .en(uc_mul_1_p7), .clk(clk), .Q(mA_q), .clr(rst));
  Register #(.width(4)) i (.D(undriven_4), .clk(clk), .Q(i_q), .clr(rst));  // open: en
  BitSelector bitselector_1 (.in(mB_q), .out(bitselector_1_out), .sel(3'b000));
  Shifter #(.shift("lr")) shifter_1 (.in(mB_q), .\dist (3'b001), .out(shifter_1_out));
  Shifter #(.width(16)) shifter_2 (.in(mA_q), .\dist (4'b0001), .out(shifter_2_out));
  Adder adder_1 ();  // open: a, b, out, cin, cout
  Comparator #(.width(1)) comparator_1 (.a(bitselector_1_out), .b(undriven_5), .eq(comparator_1_eq));  // open: gt, lt
  Adder #(.width(16)) adder_2 (.a(RES), .b(mA_q), .out(adder_2_out));  // open: cin, cout
  Multiplexer #(.width(16), .enable("false")) multiplexer_3 (
    .in0(adder_2_out), .in1({16{1'b0}}), .out(multiplexer_3_out), .sel(undriven_6));
  Register #(.width(16)) ACC (.D(multiplexer_3_out), .en(undriven_7), .clk(clk), .Q(RES), .clr(rst));
endmodule
