// Logisim project TP6.circ as structural Verilog: 2 circuits, main circuit main
module main (
  input  Rst
);

  wire Clk, Co, tp6_1_p3, tp6_1_p16, tp6_1_p17, tp6_1_p19, tp6_1_p20, tp6_1_p21, tp6_1_p22, tp6_1_p23,
       tp6_1_p24, tp6_1_p26, tp6_1_p27, tp6_1_p28, tp6_1_p30;
  wire [4:0] DECODE_1_a, DECODE_1_b, DECODE_1_r;
  wire [5:0] DECODE_1_opcod;
  wire [10:0] DECODE_1_opx;
  wire [15:0] DECODE_1_imm16;
  wire [31:0] IR_q, multiplexer_1_out, multiplexer_2_out, multiplexer_3_out, PC_q, register_file_1_p1,
       register_file_1_p9, tp6_1_p1, tp6_1_p18, tp6_1_p25;

  Clock u_clk (.out(Clk));
  // Probe on tp6_1_p18
  Register #(.width(32)) IR (.D(tp6_1_p18), .en(tp6_1_p30), .clk(Clk), .Q(IR_q), .clr(Rst));
  RAM #(.addrWidth(16), .dataWidth(32)) RAM_1 (.clr(tp6_1_p1[0]));  // open: addr, data, sel, clk, ld
  DECODE DECODE_1 (
    .IR(IR_q), .OPCOD(DECODE_1_opcod), .OPX(DECODE_1_opx), .R(DECODE_1_r), .B(DECODE_1_b), .A(DECODE_1_a),
    .IMM16(DECODE_1_imm16));
  // FSM_Entity #(.content("state_machine TP6 @[104,46,1400,800]{\n	in Zero[16]   @[104,130,70,15];One[16]   @[104,192,67,15];OPCOD[6]   @[104,229,84,15];OPX[11]   @[104,287,69,15];C[5]   @[104,331,45,15];B[5]   @[104,381,44,15];A[5]   @[104,443,44,15];IMM16[16]   @[104,500,84,15];isZero[1]   @[104,740,42,15];isNeg[1]   @[104,764,40,15];\n	out SEL0[1]   @[1465,245,39,15];RWE[1]   @[1469,296,35,15];WAD[5]   @[1439,346,65,15];RA0[5]   @[1444,392,60,15];RA1[5]   @[1444,437,60,15];PCWE[1]   @[1459,476,45,15];CST[32]   @[1437,515,67,15];SEL2[1]   @[1465,556,39,15];SEL1[1]   @[1465,596,39,15];OP[3]   @[1450,642,54,15];MEMWE[1]   @[1447,719,57,15];IRWE[1]   @[1465,749,39,15];\n	codeWidth = 6;\n	reset = IDLE;\n	\n	state IDLE[\"000001\"]:\n	 	@[181,86,30,30]\n		set OP=\"000\";  @[181,86,30,30]	\n		goto FETCH  when default   @[214,172,49,21]; \n	state FETCH[\"000000\"]:\n	 	@[245,203,30,30]\n		set CST={Zero,One};OP=\"000\";  @[245,203,30,30]	\n		goto WRITE_IR  when default   @[350,173,50,21]; \n	state Dispatch[\"000011\"]:\n	 	@[662,110,30,30]\n		goto SUB  when ((OPCOD==\"111010\").(OPX[10:5]==\"111001\"))   @[392,287,304,21]; \n		goto LDW_0  when (OPCOD==\"010111\")   @[609,229,140,21]; \n		goto STW_0  when (OPCOD==\"010101\")   @[703,272,140,21]; \n		goto BLT  when (OPCOD==\"010110\")   @[860,248,140,21]; \n		goto ADDI  when (OPCOD==\"000100\")   @[338,231,140,21]; \n		goto ILLEGAL  when default   @[792,115,50,21]; \n	state nextPC[\"000100\"]:\n	 	@[572,692,30,30]\n		set PCWE=\"1\";SEL2=\"1\";CST={Zero,One};  @[572,692,30,30]	\n		goto FETCH  when default   @[321,634,50,21]; \n	state LDW_0[\"000101\"]:\n	 	@[594,353,30,30]\n		set RA0=A;CST={Zero,IMM16};OP=\"111\";SEL1=\"1\";SEL2=\"1\";  @[594,353,30,30]	\n		goto LDW_1  when default   @[557,487,50,21]; \n	state SUB[\"000110\"]:\n	 	@[514,388,30,30]\n		set OP=\"001\";RWE=\"1\";SEL1=\"1\";RA0=A;RA1=B;WAD=C;  @[514,388,30,30]	\n		goto nextPC  when default   @[468,564,50,21]; \n	state LDW_1[\"001000\"]:\n	 	@[649,556,30,30]\n		set WAD=B;RWE=\"1\";SEL0=\"1\";  @[649,556,30,30]	\n		goto nextPC  when default   @[642,646,50,21]; \n	state STW_0[\"001001\"]:\n	 	@[789,384,30,30]\n		set RA0=A;CST={Zero,IMM16};OP=\"000\";MEMWE=\"1\";SEL1=\"0\";SEL2=\"1\";  @[789,384,30,30]	\n		goto nextPC  when default   @[794,582,50,21]; \n	state BLT[\"001011\"]:\n	 	@[918,371,30,30]\n		set RA0=A;RA1=B;OP=\"001\";SEL1=\"1\";  @[918,371,30,30]	\n		goto PC_jump  when isNeg   @[977,466,40,21]; \n		goto nextPC  when default   @[825,636,50,21]; \n	state ADDI[\"000111\"]:\n	 	@[324,377,30,30]\n		set OP=\"111\";CST={Zero,IMM16};SEL2=\"1\";RA0=A;SEL1=\"1\";SEL0=\"0\";WAD=B;RWE=\"1\";  @[324,377,30,30]	\n		goto nextPC  when default   @[397,606,50,21]; \n	state ILLEGAL[\"001010\"]:\n	 	@[1014,96,30,30]\n	state WRITE_IR[\"000010\"]:\n	 	@[423,110,30,30]\n		set IRWE=\"1\";  @[423,110,30,30]	\n		goto Dispatch  when default   @[551,121,50,21]; \n	state PC_jump[\"001100\"]:\n	 	@[1011,513,30,30]\n		set SEL1=\"0\";SEL2=\"1\";PCWE=\"1\";CST={Zero,IMM16};OP=\"111\";  @[1011,513,30,30]	\n		goto nextPC  when default   @[808,630,50,21]; \n}")) tp6_1: pin names not known; wires that end beside it: tp6_1_p1[15:0], 4'b1111, tp6_1_p3, Clk, Clk, Rst, 1'b1, {16{1'b0}}, 16'h1, DECODE_1_opcod, DECODE_1_opx, DECODE_1_r, DECODE_1_b, DECODE_1_a, DECODE_1_imm16, tp6_1_p16, tp6_1_p17, tp6_1_p18, tp6_1_p19, tp6_1_p20, tp6_1_p21, tp6_1_p22, tp6_1_p23, tp6_1_p24, tp6_1_p25, tp6_1_p26, tp6_1_p27, tp6_1_p28, tp6_1_p3, tp6_1_p30
  Multiplexer #(.width(32), .enable("false")) multiplexer_1 (
    .in0(tp6_1_p1), .in1(tp6_1_p18), .out(multiplexer_1_out), .sel(tp6_1_p19));
  // Register_File register_file_1: pin names not known; wires that end beside it: register_file_1_p1, Clk, Rst, multiplexer_1_out, tp6_1_p20, tp6_1_p21, tp6_1_p22, tp6_1_p23, register_file_1_p9, register_file_1_p1
  // Probe on tp6_1_p21
  // Probe on tp6_1_p22
  // Probe on DECODE_1_imm16
  // Probe on DECODE_1_b
  // Probe on DECODE_1_r
  // Probe on DECODE_1_opx
  // Probe on DECODE_1_opcod
  // Probe on tp6_1_p23
  Register #(.width(32)) PC (.D(tp6_1_p1), .en(tp6_1_p24), .clk(Clk), .Q(PC_q), .clr(Rst));
  // Probe on tp6_1_p25
  Multiplexer #(.width(32), .enable("false")) multiplexer_2 (
    .in0(register_file_1_p1), .in1(tp6_1_p25), .out(multiplexer_2_out), .sel(tp6_1_p26));
  // Probe on multiplexer_3_out
  Multiplexer #(.width(32), .enable("false")) multiplexer_3 (
    .in0(PC_q), .in1(register_file_1_p9), .out(multiplexer_3_out), .sel(tp6_1_p27));
  // Probe on multiplexer_2_out
  // ALU alu_1: pin names not known; wires that end beside it: multiplexer_3_out, multiplexer_2_out, Co, 1'b0, tp6_1_p16, tp6_1_p17, tp6_1_p28, tp6_1_p1
  // Probe on tp6_1_p1
  // Probe on tp6_1_p28
  // Pins of 1 and 16 bits meet at tp6_1_p1[15:0]

  // Notes on the sheet:
  //   contents of RAM_1 (hex, n*v repeats v):
  //   3c83a 5c83a 9002004 10c01017 18400056 18400004 10800044 113ffed6 8*0 10 23 13 5 45 12 23
endmodule

module DECODE (
  input  [31:0] IR,
  output [5:0] OPCOD,
  output [10:0] OPX,
  output [4:0] R,
  output [4:0] B,
  output [4:0] A,
  output [15:0] IMM16
);


  assign A = IR[31:27];
  assign B = IR[26:22];
  assign IMM16 = IR[21:6];
  assign OPCOD = IR[5:0];
  assign OPX = IR[16:6];
  assign R = IR[21:17];
endmodule
