// Logisim project TP5-6.circ as structural Verilog: 1 circuit, main circuit SYSTEM
module SYSTEM (
  input  Rst
);

  wire Clk, clr_in, clr_out, comparator_1_eq, comparator_1_gt, comparator_2_eq, comparator_2_gt, CS,
       fsm_entity_1_p7, hit, IO_ACK, IOWR_REQ, or_1_out, or_2_out, read, undriven;
  wire [6:0] char, key;
  wire [31:0] IO_ADDR, IO_DIN, undriven_2;
  wire [31:8] IO_DOUT;

  Clock u_clk (.out(Clk));
  // Nios2Simulator nios2simulator_1: pin names not known; wires that end beside it: Clk, Rst, IO_ACK, {32{1'b0}}, 1'b0
  Keyboard keyboard_1 (.clk(Clk), .re(read), .clr(clr_in), .avail(hit), .data(key));
  Comparator #(.width(32), .mode("unsigned")) comparator_1 (
    .a(IO_ADDR), .b(32'h80007040), .gt(comparator_1_gt), .eq(comparator_1_eq));  // open: lt
  Comparator #(.width(32), .mode("unsigned")) comparator_2 (
    .a(32'h80007043), .b(IO_ADDR), .gt(comparator_2_gt), .eq(comparator_2_eq));  // open: lt
  // FSM_Entity #(.content("state_machine CoupleurEcran @[50,50,800,500]{\n	in CS[1]   @[50,118,23,15];IOWR_REQ[1]   @[50,134,71,15];\n	out IO_ACK[1]   @[801,107,49,15];WRITE[1]   @[806,131,44,15];\n	codeWidth = 2;\n	reset = S0;\n	\n	state S0[\"00\"]:\n	 	@[223,232,30,30]\n		goto S1  when (CS.IOWR_REQ)   @[370,199,99,22]; \n	state S1[\"01\"]:\n	 	@[551,235,30,30]\n		set WRITE=\"1\";  @[551,235,30,30]	\n		goto S2  when default   @[559,316,43,22]; \n	state S2[\"10\"]:\n	 	@[540,362,30,30]\n		set IO_ACK=\"1\";  @[540,362,30,30]	\n		goto S0  when IOWR_REQ   @[395,320,71,22]; \n}")) fsm_entity_1: pin names not known; wires that end beside it: Clk, Rst, 1'b1, CS, IOWR_REQ, IO_ACK, fsm_entity_1_p7
  RAM #(.addrWidth(16), .dataWidth(32)) RAM_1 (.clr(IO_ADDR[2]));  // open: addr, data, sel, clk, ld
  or or_1 (or_1_out, comparator_1_gt, comparator_1_eq);
  or or_2 (or_2_out, comparator_2_gt, comparator_2_eq);
  and and_1 (CS, or_1_out, or_2_out);
  assign IO_DIN = undriven ? undriven_2 : 32'bz;  // Controlled_Buffer controlled_buffer_1
  // Probe on IO_ADDR
  // Probe on {IO_DOUT, clr_out, char}
  // Probe on IO_DIN
  TTY tty_1 (.data(char), .clk(Clk), .we(fsm_entity_1_p7), .clr(clr_out));
  // Pins of 1 and 16 bits meet at IO_ADDR[17:2]

  // Other names for the same wires on the sheet: IO_DOUT[7:0] = {clr_out, char}

  // Notes on the sheet:
  //   TP 5-6 : entrées/sorties bus
  //   Processeur NIOS
  //   Périphérique clavier
  //   contents of RAM_1 (hex, n*v repeats v):
  //   1004004 c0 3ffd26 105883a 10c00007 1809883a 2c0 18000226 10800044 3ffa26 f800283a defffe04 d9000015
  //   dfc00115 4200034 841c1004 81000025 dec00204 d9000017 dfc00117 f800283a 1200074 213fc004 21400137
  //   283ffe26 21400037 21400035 f800283a 36*0 6c6c6548 6f77206f 20646c72 6d6f7266 4f494e20 49492053
  //   6f727020 73736563 a726f 0 0 0 3f 6 5b 4f 66 6d 7d 7 7f 6f 77 7c 39 5e 79 71 65442*0 48 1c
  //   Périphérique console
endmodule
